// Logisim project Basics Gates.circ as structural Verilog: 1 circuit, main circuit main
module main (
  input  A,
  input  B,
  input  A_2,
  input  B_2,
  input  A_3
);

  wire AND_out, NOT_out, OR_out;

  and AND (AND_out, A, B);
  or OR (OR_out, A_2, B_2);
  not NOT (NOT_out, A_3);
  LED OT (.in(AND_out));
  LED OT_2 (.in(OR_out));
  LED OT_3 (.in(NOT_out));

  // Notes on the sheet:
  //                     AND Gate :-
  //              OR Gate :-
  //   NOT Gate :-
endmodule
